# Fritzing sketch CE_Dissertation (saved by Fritzing 1.0.2b)
circuit board: 5.99967cm x 3.08477cm
breadboards: 1

parts:
  A1 = ESP32 wrover cam
  U1 = LIPO-1000mAh [package=lipo-1000]  # not connected
  BME680 = BME680 Module [part_number=CJMCU-680]
  TP1 = TP4056 [chip_label=TP4056 package="DIP (Dual Inline) [THT]"]
  LED4 = LED - 3mm [color="Red (633nm)" current=30mA package="3 mm [THT]"]
  LED3 = LED - 3mm [color="Red (633nm)" current=0.030A package="3 mm [THT]"]
  R1 = Resistor [tolerance=±5% power=0.25W resistance=220 package=THT]
  R2 = Resistor [tolerance=±5% power=0.25W resistance=220 package=THT]
  S1 = Toggle Switch [package=THT]

nets (from the pcb view):
  N1: A1.Pin_1, BME680.VCC, TP1.pin3, S1.L2
  N2: A1.Pin_7, BME680.SCL
  N3: A1.Pin_8, BME680.SDA
  N4: A1.Pin_13, A1.Pin_14, A1.Pin_15, A1.Pin_29, A1.Pin_30, A1.Pin_40, BME680.GND, TP1.pin6, LED4.cathode, LED4.anode, LED3.cathode, LED3.anode, R1.Pin_0, R1.Pin_1, R2.Pin_0, R2.Pin_1
  N5: TP1.pin4, S1.COM

custom parts:
  ESP32 wrover cam: ESP32-WROVER -> A powerful and small controller with onboard camera and wireless.
  BME680 Module: Bosch BME680 Development Module The BME680 is a digital 4-in-1 sensor that measures air quality [gas], humidity, pressure and temperature. Links: BME680 product datasheet
  TP4056: A DIP stand-in part for whatever IC you want. With 6 pins on a 300mil dual inline package (DIP) footprint.
